# Fritzing sketch ejercicio-03 (saved by Fritzing 0.9.4)
breadboards: 1

parts:
  Componente1 = Arduino Uno (Rev3) - ICSP
  R1 = Resistor [tolerance=±5% resistance=10k package="0603 [SMD]"]
  S2 = Momentary Switch [package=ksa_sealed_tac_switch]

nets:
  N1: Componente1.D7, S2.4
  N2: Componente1.5V, S2.2
  N3: R1.Pin_1, S2.3
