# Fritzing sketch ejercicio-04 (saved by Fritzing 0.9.4)
breadboards: 1

parts:
  S1 = Pushbutton [package="[THT]"]
  Raspberry_Pi_1 = Raspberry Pi 3 [part_number=RPI-3-V1.2]

nets:
  N1: S1.Pin_1, S1.Pin_2, Raspberry_Pi_1.GND
  N2: S1.Pin_3, S1.Pin_4, Raspberry_Pi_1.GIPO21
