# Fritzing sketch ejercicio-06 (saved by Fritzing 0.9.4)
breadboards: 1

parts:
  Raspberry_Pi_1 = Raspberry Pi 3 [part_number=RPI-3-V1.2]
  Componente3 = Logic Level Converter
  8x8_LED_Modul_mit_MAX1 = 8x8 LED Modul mit MAX7219 [package=THT]
  YwRobot_Power_Supply1 = YwRobot Breadboard Power Supply [part_number=545043]

nets:
  N1: Raspberry_Pi_1.3v3, Componente3.LV
  N2: Raspberry_Pi_1.GPIO10, Componente3.RX_LV
  N3: Raspberry_Pi_1.GPIO11, Componente3.TX2_LV
  GND: Raspberry_Pi_1.GND, Componente3.GND, 8x8_LED_Modul_mit_MAX1.GND_Eingang, YwRobot_Power_Supply1.GND#13, YwRobot_Power_Supply1.GND#14
  N4: Raspberry_Pi_1.GPIO8, Componente3.RX2_LV
  N5: Componente3.RX_HV, 8x8_LED_Modul_mit_MAX1.DIN_Eingang
  N6: Componente3.HV, 8x8_LED_Modul_mit_MAX1.VCC_Eingang, YwRobot_Power_Supply1.VCC#9, YwRobot_Power_Supply1.VCC#10
  N7: Componente3.RX2_HV, 8x8_LED_Modul_mit_MAX1.CS_Eingang
  N8: Componente3.TX2_HV, 8x8_LED_Modul_mit_MAX1.CLK_Eingang
  N9: YwRobot_Power_Supply1.VCC#5, YwRobot_Power_Supply1.VCC#6
  N10: YwRobot_Power_Supply1.GND#11, YwRobot_Power_Supply1.GND#12

custom parts:
  YwRobot Breadboard Power Supply: The YwRobot Breadboard Power Supply (MB-V2) has two power rails; they can be 5V or 3V3. Power to the module can be provided through the female USB socket or through the A10 (female) 2.1mm power jack.
