# Fritzing sketch ejercicio-07 (saved by Fritzing 0.9.4)

parts:
  Componente1 = Arduino Uno (Rev3) - ICSP
  HC-SR04_Sensor_1 = HC-SR04 Ultrasonic Distance Sensor

nets:
  N1: Componente1.ICSP_MOSI, Componente1.D11_PWM/MOSI, HC-SR04_Sensor_1.ECHO
  N2: Componente1.D12/MISO, HC-SR04_Sensor_1.TRIG
  5V: Componente1.5V, HC-SR04_Sensor_1.VCC
  GND: Componente1.GND, HC-SR04_Sensor_1.GND
