# Fritzing sketch ejercicio-09 (saved by Fritzing 0.9.4)

parts:
  Componente1 = Arduino Uno (Rev3) - ICSP
  DHT2 = DHT11 Humitidy and Temperature Sensor (3 pins)

nets:
  N1: Componente1.D2, DHT2.VDD
  N2: Componente1.5V, DHT2.DATA
  GND: Componente1.GND, DHT2.GND

custom parts:
  DHT11 Humitidy and Temperature Sensor (3 pins): DHT11 Humidity and Temperature Sensor (3 pins) from the design created by John De Cristofaro for Adafruit Industries.
