# Fritzing sketch ejercicio-10 (saved by Fritzing 0.9.4)

parts:
  Raspberry_Pi_1 = Raspberry Pi 3 [part_number=RPI-3-V1.2]
  DHT1 = DHT11 Humitidy and Temperature Sensor (3 pins)

nets:
  N1: Raspberry_Pi_1.3v3, DHT1.DATA
  N2: Raspberry_Pi_1.GPIO21, DHT1.VDD
  GND: Raspberry_Pi_1.GND, DHT1.GND

custom parts:
  DHT11 Humitidy and Temperature Sensor (3 pins): DHT11 Humidity and Temperature Sensor (3 pins) from the design created by John De Cristofaro for Adafruit Industries.
