# Fritzing sketch ejercicio-11 (saved by Fritzing 0.9.4)

parts:
  Componente1 = Arduino Uno (Rev3) - ICSP
  S1 = H-Bridge with L298N
  M1 = DC Motor
  VCC1 = Battery

nets:
  N1: Componente1.D9_PWM, S1.IN2
  N2: Componente1.D10_PWM/SS, S1.IN1
  N3: Componente1.D11_PWM/MOSI, S1.ENA
  GND: Componente1.GND, S1.GND, VCC1.-
  5V: Componente1.5V, S1.5V
  N4: S1.12V, VCC1.+
  N5: S1.M1-01, M1.pin_2
  N6: S1.M1-02, M1.pin_1

custom parts:
  H-Bridge with L298N: h-bridge
