# Fritzing sketch ejercicio-12 (saved by Fritzing 0.9.4)

parts:
  S1 = H-Bridge with L298N
  M1 = DC Motor
  VCC1 = Battery
  Raspberry_Pi_1 = Raspberry Pi 3 [part_number=RPI-3-V1.2]

nets:
  N1: S1.12V, VCC1.+
  GND: S1.GND, VCC1.-, Raspberry_Pi_1.GND
  5V: S1.5V, Raspberry_Pi_1.5V
  N2: S1.ENA, Raspberry_Pi_1.GIPO16
  N3: S1.IN1, Raspberry_Pi_1.GIPO20
  N4: S1.IN2, Raspberry_Pi_1.GIPO21
  N5: S1.M1-01, M1.pin_2
  N6: S1.M1-02, M1.pin_1

custom parts:
  H-Bridge with L298N: h-bridge
