# Fritzing sketch ejercicio-13 (saved by Fritzing 0.9.4)

parts:
  X1 = X113647 Stepper Driver Board [part_number=X113647 package=board]
  Part1 = Arduino Uno (Rev3)
  MOTOR1 = 28BYJ-48 Stepper Motor

nets:
  N1: X1.IN1, Part1.D8
  N2: X1.IN2, Part1.D9_PWM
  N3: X1.IN3, Part1.D10_PWM/SS
  N4: X1.IN4, Part1.D11_PWM/MOSI
  GND: X1.GND, Part1.GND
  HVCC/VCC: X1.+V, Part1.5V
  N5: X1.BLUE, MOTOR1.BLUE
  N6: X1.PINK, MOTOR1.PINK
  N7: X1.YELLOW, MOTOR1.YELLOW
  N8: X1.ORANGE, MOTOR1.ORANGE
  N9: X1.RED, MOTOR1.RED

custom parts:
  X113647 Stepper Driver Board: A common stepper motor driver board based on ULN2003APG darlington array
  28BYJ-48 Stepper Motor: 28BYJ-48 gear-reduction stepper motor (small)
