# Fritzing sketch ejercicio-14 (saved by Fritzing 0.9.4)
breadboards: 1

parts:
  MOTOR1 = 28BYJ-48 Stepper Motor
  X1 = X113647 Stepper Driver Board [part_number=X113647 package=board]
  Raspberry_Pi_1 = Raspberry Pi 3 [part_number=RPI-3-V1.2]
  YwRobot_Power_Supply1 = YwRobot Breadboard Power Supply [part_number=545043]  # not connected

nets:
  N1: MOTOR1.BLUE, X1.BLUE
  N2: MOTOR1.PINK, X1.PINK
  N3: MOTOR1.RED, X1.RED
  N4: MOTOR1.ORANGE, X1.ORANGE
  N5: MOTOR1.YELLOW, X1.YELLOW
  GND/HVCC: X1.IN1, X1.GND, X1.+V, Raspberry_Pi_1.GND, Raspberry_Pi_1.GIPO12
  N6: X1.IN2, Raspberry_Pi_1.GIPO16
  N7: X1.IN3, Raspberry_Pi_1.GIPO20
  N8: X1.IN4, Raspberry_Pi_1.GIPO21

custom parts:
  28BYJ-48 Stepper Motor: 28BYJ-48 gear-reduction stepper motor (small)
  X113647 Stepper Driver Board: A common stepper motor driver board based on ULN2003APG darlington array
  YwRobot Breadboard Power Supply: The YwRobot Breadboard Power Supply (MB-V2) has two power rails; they can be 5V or 3V3. Power to the module can be provided through the female USB socket or through the A10 (female) 2.1mm power jack.
