# Fritzing sketch ejercicio-15 (saved by Fritzing 0.9.4)

parts:
  Componente1 = Arduino Uno (Rev3) - ICSP
  J1 = Basic Servo

nets:
  N1: Componente1.D9_PWM, J1.pulse
  GND: Componente1.GND, J1.gnd
  5V: Componente1.5V, J1.vcc
