# Fritzing sketch ejercicio-16 (saved by Fritzing 0.9.4)

parts:
  Raspberry_Pi_1 = Raspberry Pi 3 [part_number=RPI-3-V1.2]
  J1 = Basic Servo
  VCC1 = Battery

nets:
  GND: Raspberry_Pi_1.GND, J1.gnd, VCC1.-
