# Fritzing sketch practica-02 (saved by Fritzing 0.9.4)
breadboards: 1

parts:
  Componente1 = Arduino Uno (Rev3) - ICSP
  R1 = Resistor [tolerance=±5% resistance=10k package="0603 [SMD]"]
  S2 = Momentary Switch [package=ksa_sealed_tac_switch]
  Raspberry_Pi_1 = Raspberry Pi 3 [part_number=RPI-3-V1.2]
  S3 = Pushbutton [package="[SMD]"]
  R2 = Resistor [tolerance=±5% resistance=10k package="0402 [SMD]"]
  Componente2 = Logic Level Converter

nets:
  N1: Componente1.D8, R1.Pin_1, S2.1, S2.3
  GND: Componente1.GND, R1.Pin_0, Raspberry_Pi_1.GND, R2.Pin_0, Componente2.GND
  N2: Componente1.D0/RX, Componente2.TX_HV
  N3: Componente1.D1/TX, Componente2.RX_HV
  N4: Componente1.D7, S3.Pin_1, S3.Pin_2, S3.Pin_3, S3.Pin_4, R2.Pin_1
  N5: Componente1.5V, Componente2.HV
  N6: S2.2, S2.4
  N7: Raspberry_Pi_1.3v3, Componente2.LV
  N8: Raspberry_Pi_1.GIPO15, Componente2.RX_LV
  N9: Raspberry_Pi_1.GIPO14, Componente2.TX_LV
