# Fritzing sketch practica-04 (saved by Fritzing 0.9.4)

parts:
  Componente1 = Arduino Uno (Rev3) - ICSP
  Raspberry_Pi_1 = Raspberry Pi 3 [part_number=RPI-3-V1.2]
  Componente3 = Logic Level Converter
  HC-SR04_Sensor_1 = HC-SR04 Ultrasonic Distance Sensor

nets:
  N1: Componente1.D11_PWM/MOSI, HC-SR04_Sensor_1.ECHO
  N2: Componente1.D12/MISO, HC-SR04_Sensor_1.TRIG
  GND: Componente1.GND, Raspberry_Pi_1.GND, Componente3.GND, HC-SR04_Sensor_1.GND
  N3: Componente1.D0/RX, Componente3.RX2_HV
  N4: Componente1.D1/TX, Componente3.TX2_HV
  5V: Componente1.5V, Componente3.HV, HC-SR04_Sensor_1.VCC
  N5: Raspberry_Pi_1.3v3, Componente3.LV
  N6: Raspberry_Pi_1.GPIO15, Componente3.TX2_LV
  N7: Raspberry_Pi_1.GPIO14, Componente3.RX2_LV
