# Fritzing sketch practica-07 (saved by Fritzing 0.9.4)
breadboards: 1

parts:
  MOTOR1 = 28BYJ-48 Stepper Motor
  X1 = X113647 Stepper Driver Board [part_number=X113647 package=board]
  Raspberry_Pi_1 = Raspberry Pi 3 [part_number=RPI-3-V1.2]
  YwRobot_Power_Supply1 = YwRobot Breadboard Power Supply [part_number=545043]  # not connected
  Componente1 = Arduino Uno (Rev3) - ICSP
  Componente2 = I2C level shifter bidirectional

nets:
  N1: MOTOR1.BLUE, X1.BLUE
  N2: MOTOR1.PINK, X1.PINK
  N3: MOTOR1.RED, X1.RED
  N4: MOTOR1.ORANGE, X1.ORANGE
  N5: MOTOR1.YELLOW, X1.YELLOW
  N6: X1.IN1, Componente1.D8
  N7: X1.IN2, Componente1.D9_PWM
  N8: X1.IN3, Componente1.D10_PWM/SS
  N9: X1.IN4, Componente1.D11_PWM/MOSI
  GND/HVCC: X1.GND, X1.+V, Raspberry_Pi_1.GND, Componente1.GND, Componente2.GND
  N10: Raspberry_Pi_1.3V3, Componente2.LV
  N11: Raspberry_Pi_1.GIPO15, Componente2.LV4
  N12: Raspberry_Pi_1.GIPO14, Componente2.LV3
  N13: Componente1.D0/RX, Componente2.HV3
  N14: Componente1.D1/TX, Componente2.HV4
  N15: Componente1.5V, Componente2.HV

custom parts:
  28BYJ-48 Stepper Motor: 28BYJ-48 gear-reduction stepper motor (small)
  X113647 Stepper Driver Board: A common stepper motor driver board based on ULN2003APG darlington array
  YwRobot Breadboard Power Supply: The YwRobot Breadboard Power Supply (MB-V2) has two power rails; they can be 5V or 3V3. Power to the module can be provided through the female USB socket or through the A10 (female) 2.1mm power jack.
