# Fritzing sketch practica-09 (saved by Fritzing 0.9.4)

parts:
  Componente1 = Arduino Uno (Rev3) - ICSP
  Raspberry_Pi_1 = Raspberry Pi 3 [part_number=RPI-3-V1.2]
  Componente3 = Logic Level Converter
  Squix1 = OLED 0.96" 128x64 I2C SSD1306

nets:
  N1: Componente1.A4/SDA, Squix1.SCA
  N2: Componente1.A5/SCL, Squix1.SCL
  GND: Componente1.GND, Raspberry_Pi_1.GND, Componente3.GND
  N3: Componente1.D0/RX, Componente3.RX2_HV
  N4: Componente1.D1/TX, Componente3.TX2_HV
  N5: Componente1.5V, Componente3.HV
  N6: Raspberry_Pi_1.3v3, Componente3.LV
  N7: Raspberry_Pi_1.GPIO15, Componente3.TX2_LV
  N8: Raspberry_Pi_1.GPIO14, Componente3.RX2_LV
