# Fritzing sketch dc2 (saved by Fritzing 0.9.4)

parts:
  Componente1 = Arduino Uno (Rev3) - ICSP
  S1 = H-Bridge with L298N
  M1 = DC Motor
  VCC1 = Battery
  Raspberry_Pi_1 = Raspberry Pi 3 [part_number=RPI-3-V1.2]
  Componente3 = Logic Level Converter

nets:
  N1: Componente1.D9_PWM, S1.IN2
  N2: Componente1.D10_PWM/SS, S1.IN1
  N3: Componente1.D11_PWM/MOSI, S1.ENA
  GND: Componente1.GND, S1.GND, VCC1.-, Raspberry_Pi_1.GND, Componente3.GND
  N4: Componente1.D0/RX, Componente3.RX2_HV
  N5: Componente1.D1/TX, Componente3.TX2_HV
  5V: Componente1.5V, S1.5V, Componente3.HV
  N6: S1.12V, VCC1.+
  N7: S1.M1-01, M1.pin_2
  N8: S1.M1-02, M1.pin_1
  N9: Raspberry_Pi_1.3v3, Componente3.LV
  N10: Raspberry_Pi_1.GIPO15, Componente3.TX2_LV
  N11: Raspberry_Pi_1.GIPO14, Componente3.RX2_LV

custom parts:
  H-Bridge with L298N: h-bridge
