# Fritzing sketch dht12 (saved by Fritzing 0.9.4)

parts:
  Componente1 = Arduino Uno (Rev3) - ICSP
  Raspberry_Pi_1 = Raspberry Pi 3 [part_number=RPI-3-V1.2]
  Componente3 = Logic Level Converter
  DHT1 = DHT11 Humitidy and Temperature Sensor (3 pins)

nets:
  GND: Componente1.GND, Raspberry_Pi_1.GND, Componente3.GND, DHT1.GND
  N1: Componente1.D0/RX, Componente3.RX2_HV
  N2: Componente1.D1/TX, Componente3.TX2_HV
  N3: Componente1.D2, DHT1.VDD
  N4: Componente1.5V, Componente3.HV, DHT1.DATA
  N5: Raspberry_Pi_1.3v3, Componente3.LV
  N6: Raspberry_Pi_1.GPIO15, Componente3.TX2_LV
  N7: Raspberry_Pi_1.GPIO14, Componente3.RX2_LV

custom parts:
  DHT11 Humitidy and Temperature Sensor (3 pins): DHT11 Humidity and Temperature Sensor (3 pins) from the design created by John De Cristofaro for Adafruit Industries.
