# Fritzing sketch led-rgb (saved by Fritzing 0.9.4)
breadboards: 1

parts:
  LED1 = RGB LED (com. anode, rbg) [package="5 mm [THT]"]
  Componente1 = Arduino Uno (Rev3) - ICSP
  R1 = Resistor [tolerance=±5% resistance=220 package="1206 [SMD]"]
  R2 = Resistor [tolerance=±5% resistance=220 package="1206 [SMD]"]
  R3 = Resistor [tolerance=±5% resistance=220 package="1206 [SMD]"]

nets:
  N1: LED1.red_cathode, R1.Pin_0
  N2: LED1.common_anode, Componente1.GND
  N3: LED1.blue_cathode, R2.Pin_0
  N4: LED1.green_cathode, R3.Pin_0
  N5: Componente1.D3_PWM, R3.Pin_1
  N6: Componente1.D5_PWM, R2.Pin_1
  N7: Componente1.D6_PWM, R1.Pin_1
