# Fritzing sketch led_rgb_3 (saved by Fritzing 0.9.4)
breadboards: 1

parts:
  Raspberry_Pi_1 = Raspberry Pi 3 [part_number=RPI-3-V1.2]
  LED1 = RGB LED (com. anode, rbg) [package="5 mm [THT]"]
  R1 = Resistor [tolerance=±5% resistance=220 package="2010 [SMD]"]
  R2 = Resistor [tolerance=±5% resistance=220 package="2010 [SMD]"]
  R3 = Resistor [tolerance=±5% resistance=220 package="2010 [SMD]"]

nets:
  N1: Raspberry_Pi_1.GPIO21, R3.Pin_1
  N2: Raspberry_Pi_1.GPIO20, R2.Pin_1
  N3: Raspberry_Pi_1.GPIO16, R1.Pin_1
  N4: Raspberry_Pi_1.GND, LED1.common_anode
  N5: LED1.red_cathode, R1.Pin_0
  N6: LED1.blue_cathode, R2.Pin_0
  N7: LED1.green_cathode, R3.Pin_0
