# Fritzing sketch hc_sr043 (saved by Fritzing 0.9.4)
breadboards: 1

parts:
  Raspberry_Pi_1 = Raspberry Pi 3 [part_number=RPI-3-V1.2]
  Componente3 = Logic Level Converter
  HC-SR04_Sensor_1 = HC-SR04 Ultrasonic Distance Sensor
  YwRobot_Power_Supply1 = YwRobot Breadboard Power Supply [part_number=545043]

nets:
  N1: Raspberry_Pi_1.3v3, Componente3.LV
  N2: Raspberry_Pi_1.GPIO21, Componente3.TX2_LV
  N3: Raspberry_Pi_1.GPIO20, Componente3.RX2_LV
  GND: Raspberry_Pi_1.GND, Componente3.GND, HC-SR04_Sensor_1.GND, YwRobot_Power_Supply1.GND#13, YwRobot_Power_Supply1.GND#14
  N4: Componente3.HV, HC-SR04_Sensor_1.VCC, YwRobot_Power_Supply1.VCC#9, YwRobot_Power_Supply1.VCC#10
  N5: Componente3.RX2_HV, HC-SR04_Sensor_1.TRIG
  N6: Componente3.TX2_HV, HC-SR04_Sensor_1.ECHO
  N7: YwRobot_Power_Supply1.VCC#5, YwRobot_Power_Supply1.VCC#6
  N8: YwRobot_Power_Supply1.GND#11, YwRobot_Power_Supply1.GND#12

custom parts:
  YwRobot Breadboard Power Supply: The YwRobot Breadboard Power Supply (MB-V2) has two power rails; they can be 5V or 3V3. Power to the module can be provided through the female USB socket or through the A10 (female) 2.1mm power jack.
