# Fritzing sketch max72192 (saved by Fritzing 0.9.4)

parts:
  Componente1 = Arduino Uno (Rev3) - ICSP
  Raspberry_Pi_1 = Raspberry Pi 3 [part_number=RPI-3-V1.2]
  Componente3 = Logic Level Converter
  8x8_LED_Modul_mit_MAX1 = 8x8 LED Modul mit MAX7219 [package=THT]

nets:
  N1: Componente1.D10_PWM/SS, 8x8_LED_Modul_mit_MAX1.CS_Eingang
  N2: Componente1.D11_PWM/MOSI, 8x8_LED_Modul_mit_MAX1.CLK_Eingang
  N3: Componente1.D12/MISO, 8x8_LED_Modul_mit_MAX1.DIN_Eingang
  GND: Componente1.GND, Raspberry_Pi_1.GND, Componente3.GND, 8x8_LED_Modul_mit_MAX1.GND_Eingang
  N4: Componente1.D0/RX, Componente3.RX2_HV
  N5: Componente1.D1/TX, Componente3.TX2_HV
  N6: Componente1.5V, Componente3.HV, 8x8_LED_Modul_mit_MAX1.VCC_Eingang
  N7: Raspberry_Pi_1.3v3, Componente3.LV
  N8: Raspberry_Pi_1.GPIO15, Componente3.TX2_LV
  N9: Raspberry_Pi_1.GPIO14, Componente3.RX2_LV
