# Fritzing sketch max72193 (saved by Fritzing 0.9.4)

parts:
  Raspberry_Pi_1 = Raspberry Pi 3 [part_number=RPI-3-V1.2]
  Componente3 = Logic Level Converter
  8x8_LED_Modul_mit_MAX1 = 8x8 LED Modul mit MAX7219 [package=THT]  # not connected

nets:
  N1: Raspberry_Pi_1.3v3, Componente3.LV
  GND: Raspberry_Pi_1.GND, Componente3.GND
  N2: Raspberry_Pi_1.GPIO15, Componente3.TX2_LV
  N3: Raspberry_Pi_1.GPIO14, Componente3.RX2_LV
