# Fritzing sketch oled3 (saved by Fritzing 0.9.4)

parts:
  Raspberry_Pi_1 = Raspberry Pi 3 [part_number=RPI-3-V1.2]
  Componente3 = Logic Level Converter
  Squix1 = OLED 0.96" 128x64 I2C SSD1306
  VCC1 = 4 x AAA Battery Mount

nets:
  N1: Raspberry_Pi_1.3v3, Componente3.LV
  N2: Raspberry_Pi_1.GPIO2, Componente3.TX2_LV
  N3: Raspberry_Pi_1.GPIO3, Componente3.RX2_LV
  GND: Raspberry_Pi_1.GND, Componente3.GND
  N4: Componente3.HV, Squix1.VCC
  N5: Componente3.RX2_HV, Squix1.SCL
  N6: Componente3.TX2_HV, Squix1.SCA
  N7: Squix1.GND, VCC1.-
