# Fritzing sketch parctica-01 (saved by Fritzing 0.9.4)
breadboards: 1

parts:
  Componente1 = Arduino Uno (Rev3) - ICSP
  Raspberry_Pi_1 = Raspberry Pi 3 [part_number=RPI-3-V1.2]
  LED1 = RGB LED (com. anode, rbg) [package="5 mm [THT]"]
  R1 = Resistor [tolerance=±5% resistance=220 package="2010 [SMD]"]
  R2 = Resistor [tolerance=±5% resistance=220 package="2010 [SMD]"]
  R3 = Resistor [tolerance=±5% resistance=220 package="2010 [SMD]"]
  Componente3 = Logic Level Converter

nets:
  GND: Componente1.GND, Raspberry_Pi_1.GND, LED1.common_anode, Componente3.GND
  N1: Componente1.D0/RX, Componente3.RX2_HV
  N2: Componente1.D1/TX, Componente3.TX2_HV
  N3: Componente1.D3_PWM, R3.Pin_1
  N4: Componente1.D5_PWM, R2.Pin_1
  N5: Componente1.D6_PWM, R1.Pin_1
  N6: Componente1.5V, Componente3.HV
  N7: Raspberry_Pi_1.3v3, Componente3.LV
  N8: Raspberry_Pi_1.GPIO15, Componente3.TX2_LV
  N9: Raspberry_Pi_1.GPIO14, Componente3.RX2_LV
  N10: LED1.red_cathode, R1.Pin_0
  N11: LED1.blue_cathode, R2.Pin_0
  N12: LED1.green_cathode, R3.Pin_0
