# Fritzing sketch serial-01 (saved by Fritzing 0.9.4)

parts:
  Componente1 = Arduino Uno (Rev3) - ICSP
  Raspberry_Pi_1 = Raspberry Pi 3 [part_number=RPI-3-V1.2]
  Componente2 = Logic Level Converter

nets:
  GND: Componente1.GND, Raspberry_Pi_1.GND, Componente2.GND
  N1: Componente1.D0/RX, Componente2.RX_HV
  N2: Componente1.D1/TX, Componente2.TX_HV
  N3: Componente1.5V, Componente2.HV
  N4: Raspberry_Pi_1.3v3, Componente2.LV
  N5: Raspberry_Pi_1.GIPO15, Componente2.TX_LV
  N6: Raspberry_Pi_1.GIPO14, Componente2.RX_LV
